# Fritzing sketch Layout_slave_board_V2_comm (saved by Fritzing 0.9.2b)

parts:
  Part3 = Arduino Nano (Rev3.0)
  Part4 = Arduino Nano (Rev3.0)
  S1 = H-Bridge with L298N
  J44 = double row male pin header, 20 pins [form="♂ (male)"]
  J45 = shrouded pin header, 40 pins [form="♂ (shrouded male)"]  # not connected
  J1 = male pin header, 6 pins [form="♂ (male)"]
  J7 = male pin header, 2 pins [form="♂ (male)"]
  J6 = male pin header, 2 pins [form="♂ (male)"]
  J5 = male pin header, 2 pins [form="♂ (male)"]
  J4 = male pin header, 2 pins [form="♂ (male)"]
  Part5 = Arduino Nano (Rev3.0)
  Part6 = Arduino Nano (Rev3.0)
  J46 = male pin header, 6 pins [form="♂ (male)"]
  J47 = male pin header, 2 pins [form="♂ (male)"]
  J48 = male pin header, 2 pins [form="♂ (male)"]
  J49 = male pin header, 2 pins [form="♂ (male)"]
  J50 = male pin header, 2 pins [form="♂ (male)"]
  S2 = H-Bridge with L298N
  Part7 = Arduino Nano (Rev3.0)
  Part8 = Arduino Nano (Rev3.0)
  J51 = male pin header, 6 pins [form="♂ (male)"]
  J52 = male pin header, 2 pins [form="♂ (male)"]
  J53 = male pin header, 2 pins [form="♂ (male)"]
  J54 = male pin header, 2 pins [form="♂ (male)"]
  J55 = male pin header, 2 pins [form="♂ (male)"]
  S3 = H-Bridge with L298N
  J56 = shrouded pin header, 10 pins [form="♂ (shrouded male)"]
  J15 = shrouded pin header, 10 pins [form="♂ (shrouded male)"]
  J57 = male pin header, 1 pin [form="♂ (male)"]
  J58 = male pin header, 1 pin [form="♂ (male)"]
  D1 = Rectifier Diode [part_number=1N4001 package="300 mil [THT]"]
  D2 = Rectifier Diode [part_number=1N4001 package="300 mil [THT]"]
  D3 = Rectifier Diode [part_number=1N4001 package="300 mil [THT]"]
  D4 = Rectifier Diode [part_number=1N4001 package="300 mil [THT]"]
  J63 = male pin header, 1 pin [form="♂ (male)"]
  J64 = male pin header, 1 pin [form="♂ (male)"]
  J65 = male pin header, 1 pin [form="♂ (male)"]
  J66 = male pin header, 1 pin [form="♂ (male)"]
  R1 = Resistor [tolerance=±5% resistance=220 package=THT]
  J68 = male pin header, 1 pin [form="♂ (male)"]
  J69 = male pin header, 1 pin [form="♂ (male)"]
  D5 = Rectifier Diode [part_number=1N4001 package="300 mil [THT]"]
  J71 = male pin header, 1 pin [form="♂ (male)"]
  D6 = Rectifier Diode [part_number=1N4001 package="300 mil [THT]"]
  J74 = male pin header, 2 pins [form="♂ (male)"]
  J75 = male pin header, 2 pins [form="♂ (male)"]
  J76 = male pin header, 2 pins [form="♂ (male)"]
  J77 = male pin header, 2 pins [form="♂ (male)"]
  J78 = male pin header, 2 pins [form="♂ (male)"]
  J79 = male pin header, 2 pins [form="♂ (male)"]
  J80 = shrouded pin header, 10 pins [form="♂ (shrouded male)"]
  J81 = shrouded pin header, 10 pins [form="♂ (shrouded male)"]
  J43 = male pin header, 20 pins [form="♂ (male)"]
  J42 = male pin header, 20 pins [form="♂ (male)"]
  Part10 = Arduino Nano (Rev3.0)
  J83 = male pin header, 2 pins [form="♂ (male)"]
  J84 = male pin header, 2 pins [form="♂ (male)"]
  S4 = H-Bridge with L298N
  D8 = Rectifier Diode [part_number=1N4001 package="300 mil [THT]"]
  J88 = male pin header, 1 pin [form="♂ (male)"]
  J90 = male pin header, 2 pins [form="♂ (male)"]
  J92 = shrouded pin header, 10 pins [form="♂ (shrouded male)"]
  J82 = male pin header, 3 pins [form="♂ (male)"]
  J85 = male pin header, 4 pins [form="♂ (male)"]
  J93 = male pin header, 1 pin [form="♂ (male)"]
  J94 = male pin header, 1 pin [form="♂ (male)"]
  J95 = male pin header, 1 pin [form="♂ (male)"]
  J98 = male pin header, 1 pin [form="♂ (male)"]
  J99 = male pin header, 1 pin [form="♂ (male)"]
  J100 = male pin header, 1 pin [form="♂ (male)"]
  J101 = male pin header, 1 pin [form="♂ (male)"]
  J104 = double row female pin header, 20 pins [form="♀ (female)"]
  U4 = mystery part, 9 pins [chip_label=R-net]
  U6 = mystery part, 12 pins [chip_label=C-group]
  J105 = male pin header, 20 pins [form="♂ (male)"]
  U5 = mystery part, 12 pins [chip_label=R-D-group]

nets:
  N1: Part3.D1/TX, D3.cathode
  N2: Part3.D0/RX, J76.pin1
  N3: Part3.RESET, Part4.RESET, Part5.RESET, Part6.RESET, J80.pin6
  N4: Part3.D2, J7.pin1, J6.pin1, J43.pin15, J42.pin6
  N5: Part3.D3, J44.pin15, J7.pin2, J6.pin2
  N6: Part3.D4, S1.ENA, J1.pin1
  N7: Part3.D10, S1.IN2, J1.pin3
  N8: Part3.D11/MOSI, S1.IN1, J1.pin2
  N9: Part3.D12/MISO, J80.pin7
  N10: Part4.D1/TX, D4.cathode
  N11: Part4.D0/RX, J77.pin1
  N12: Part4.D2, J5.pin1, J4.pin1, J43.pin12, J42.pin9
  N13: Part4.D3, J44.pin12, J5.pin2, J4.pin2
  N14: Part4.D4, S1.ENB, J1.pin6
  N15: Part4.D10, S1.IN4, J1.pin5
  N16: Part4.D11/MOSI, S1.IN3, J1.pin4
  N17: Part4.D12/MISO, J80.pin3
  N18: Part4.5V, R1.Pin_0
  N19: S1.M1-01, J43.pin6, J42.pin15
  N20: S1.M1-02, J44.pin6
  N21: S1.M2-01, J44.pin3
  N22: S1.M2-02, J43.pin3, J42.pin18
  N23: J44.pin1, S2.M1-02
  N24: J44.pin2, S2.M2-01
  N25: J44.pin4, J15.pin3
  N26: J44.pin5, J15.pin4
  N27: J44.pin7, J57.pin1, J43.pin7, J42.pin13, J42.pin14
  N28: J44.pin8, J44.pin9, J58.pin1, J43.pin9, J42.pin12
  N29: J44.pin10, Part5.D3, J49.pin2, J50.pin2
  N30: J44.pin11, Part6.D3, J47.pin2, J48.pin2
  N31: J44.pin13, J15.pin1
  N32: J44.pin14, J15.pin2
  N33: Part5.D1/TX, D1.cathode
  N34: Part5.D0/RX, J74.pin1
  N35: Part5.D2, J49.pin1, J50.pin1, J43.pin10, J42.pin11
  N36: Part5.D4, J46.pin1, S2.ENA, S2.ENA-5V
  N37: Part5.D10, J46.pin3, S2.IN2
  N38: Part5.D11/MOSI, J46.pin2, S2.IN1
  N39: Part5.D12/MISO, J80.pin8
  N40: Part6.D1/TX, D2.cathode
  N41: Part6.D0/RX, J75.pin1
  N42: Part6.D2, J47.pin1, J48.pin1, J43.pin11, J42.pin10
  N43: Part6.D4, J46.pin6, S2.ENB, S2.ENB-5V
  N44: Part6.D10, J46.pin5, S2.IN4
  N45: Part6.D11/MOSI, J46.pin4, S2.IN3
  N46: Part6.D12/MISO, J80.pin4
  N47: S2.M1-01, J43.pin1, J42.pin20
  N48: S2.M2-02, J43.pin2, J42.pin19
  N49: Part7.D1/TX, D6.cathode
  N50: Part7.D0/RX, J78.pin1
  N51: Part7.RESET, Part8.RESET, J81.pin6
  N52: Part7.GND, Part7.D2, J54.pin1, J55.pin1, J56.pin2
  N53: Part7.D3, J54.pin2, J55.pin2, J56.pin9
  N54: Part7.D4, J51.pin1, S3.ENA, S3.ENA-5V
  N55: Part7.D9, Part7.D10, J51.pin3, S3.IN2
  N56: Part7.D11/MOSI, J51.pin2, S3.IN1
  N57: Part7.D12/MISO, J81.pin8
  N58: Part8.D1/TX, D5.cathode
  N59: Part8.D0/RX, J79.pin1
  N60: Part8.D2, J52.pin1, J53.pin1, J56.pin1
  N61: Part8.D3, J52.pin2, J53.pin2, J56.pin10
  N62: Part8.D4, J51.pin6, S3.ENB
  N63: Part8.D9, Part8.D10, J51.pin5, S3.IN4
  N64: Part8.D11/MOSI, J51.pin4, S3.IN3
  N65: Part8.D12/MISO, J81.pin3
  N66: S3.M1-01, J56.pin4
  N67: S3.M1-02, J56.pin7
  N68: S3.M2-01, J56.pin8
  N69: S3.M2-02, J56.pin3
  N70: J15.pin7, J43.pin5, J42.pin16
  N71: J15.pin8, J43.pin4, J42.pin17
  N72: J15.pin9, J43.pin14, J42.pin7
  N73: J15.pin10, J43.pin13, J42.pin8
  N74: D1.anode, D2.anode, D3.anode, D4.anode, J63.pin1, J64.pin1, J65.pin1, J66.pin1, R1.Pin_1, J68.pin1, J80.pin10
  N75: J69.pin1, D5.anode, J71.pin1, D6.anode, J81.pin10
  N76: J74.pin2, J75.pin2, J76.pin2, J77.pin2, J80.pin1
  N77: J78.pin2, J79.pin2, J81.pin1
  N78: J80.pin2, J101.pin1
  N79: J80.pin9, J100.pin1
  N80: J81.pin2, J99.pin1
  N81: J81.pin9, J98.pin1
  N82: Part10.D1/TX, D8.cathode
  N83: Part10.D0/RX, J90.pin1
  N84: Part10.RESET, J92.pin6, J92.pin7
  N85: Part10.D2, J83.pin1, J84.pin1, J85.pin2, J85.pin3, J93.pin1
  N86: Part10.D3, J83.pin2, J84.pin2, J85.pin4
  N87: Part10.D4, S4.ENA, S4.ENB, S4.ENA-5V, J82.pin3
  N88: Part10.D9, Part10.D10, S4.IN2, S4.IN4, J82.pin2
  N89: Part10.D11/MOSI, S4.IN1, S4.IN3, J82.pin1
  N90: Part10.D12/MISO, J92.pin3
  N91: S4.M1-01, S4.M2-02
  N92: S4.M1-02, S4.M2-01
  N93: D8.anode, J92.pin10
  N94: J88.pin1, J85.pin1
  N95: J90.pin2, J92.pin1
  N96: J92.pin2, J94.pin1
  N97: J92.pin9, J95.pin1
  N98: J104.pin6, U6.pin1, U5.pin12
  N99: J104.pin7, U6.pin2, U5.pin11
  N100: J104.pin8, U6.pin3, U5.pin10
  N101: J104.pin9, U6.pin4, U5.pin9
  N102: J104.pin10, U6.pin5, U5.pin8
  N103: J104.pin11, U6.pin6, U5.pin7
  N104: J104.pin12, J104.pin13, U6.pin12, J105.pin12, J105.pin13
  N105: J104.pin14, U4.pin9, J105.pin14
  N106: U4.pin3, J105.pin6, U5.pin1
  N107: U4.pin4, J105.pin7, U5.pin2
  N108: U4.pin5, J105.pin8, U5.pin3
  N109: U4.pin6, J105.pin9, U5.pin4
  N110: U4.pin7, J105.pin10, U5.pin5
  N111: U4.pin8, J105.pin11, U5.pin6

notes:
  UAJ
  SKG
  SKF
  SKE
  Shoulder
  UAE
  Master
  Z-Achse
  filter

custom parts:
  H-Bridge with L298N: h-bridge
