# Fritzing sketch SKE_Originalverkabelung (saved by Fritzing 0.9.3b)

parts:
  RP7 = Resistor [tolerance=±5% resistance=1k package=THT]
  RP8 = Resistor [tolerance=±5% resistance=1k package=THT]
  D5 = Rectifier Diode [part_number=1N4148 package="300 mil [THT]"]
  C7 = Ceramic Capacitor [capacitance=4.7nF package="100 mil [THT, multilayer]"]
  RP7_2 = Resistor [tolerance=±5% resistance=1k package=THT]
  RP8_2 = Resistor [tolerance=±5% resistance=1k package=THT]
  D6 = Rectifier Diode [part_number=1N4148 package="300 mil [THT]"]
  IC29 = 4071 4 x 2 Input OR Gate, single part [part_number=SN74LS86N package="DIP (Dual Inline) [THT]"]
  SKE-gelb = PHOTOTRANSISTOR REFLECTIVE OBJECT SENSOR [package=qrb1114-side]
  SKE-weis = PHOTOTRANSISTOR REFLECTIVE OBJECT SENSOR [package=qrb1114-side]
  C8 = Ceramic Capacitor [capacitance=4.7nF package="100 mil [THT, multilayer]"]

nets:
  5V: RP7.Pin_0, RP7_2.Pin_0
  N1: RP7.Pin_1, RP8.Pin_0, D5.anode, SKE-gelb.C
  N2: RP8.Pin_1, D5.cathode, IC29.A1, C8.1
  GND: C7.0, SKE-gelb.E, SKE-weis.E, C8.0
  N3: C7.1, RP8_2.Pin_1, D6.cathode, IC29.B1, IC29.A2
  N4: RP7_2.Pin_1, RP8_2.Pin_0, D6.anode, SKE-weis.C
  IO1: IC29.Q1
  IO18: IC29.B2

notes:
  logic -->
  ~1.5m Leitung
